# Fritzing sketch enc28j60 (saved by Fritzing 0.9.2b)
circuit board: 4.40476cm x 5.84116cm
breadboards: 1

parts:
  Sensor = female alternating pin header, 3 pins [form="♀ (female)"]
  Fonte = male pin header, 2 pins [form="♂ (male)"]
  Enc28j60 = ENC28J60 Breakout Board
  Arduino = Arduino Nano (Rev3.0)

nets:
  GND: Sensor.pin1, Fonte.pin1, Enc28j60.GND, Arduino.GND
  N1: Sensor.pin2, Arduino.D3
  VCC: Sensor.pin3, Enc28j60.VCC, Arduino.5V
  N2: Fonte.pin2, Arduino.VIN
  N3: Enc28j60.CS, Arduino.D10
  N4: Enc28j60.SI, Arduino.D11/MOSI
  N5: Enc28j60.SCK, Arduino.D13/SCK
  N6: Enc28j60.SO, Arduino.D12/MISO
  N7: Enc28j60.INT, Arduino.D2

custom parts:
  ENC28J60 Breakout Board: This is a breakout board for the Microchip ENC28J60 stand-alone ethernet controller. The ENC28J60 has an SPI interface. It operates at 3.3 Volts.
