# Fritzing sketch schematic (saved by Fritzing 0.9.2b)
circuit board: 4.47087cm x 3.29762cm
breadboards: 1

parts:
  C1 = Electrolytic Capacitor [part_number=1 package="100 mil [THT, electrolytic]"]
  ESP8266 = shrouded pin header, 8 pins [form="♂ (shrouded male)"]
  R2 = Resistor [tolerance=±5% resistance=240 part_number=5 package=THT]
  USBSerial = female pin header, 5 pins [form="♀ (female)" part_number=6]
  R1 = Resistor [tolerance=±5% resistance=390 part_number=4 package=THT]
  U1 = Voltage Regulator [part_number=2 package=to220-adj]
  Sensor = male pin header, 3 pins [form="♂ (male)"]
  C2 = Electrolytic Capacitor [capacitance=10µF package="100 mil [THT, electrolytic]"]
  J4 = male pin header, 3 pins [form="♂ (male)"]
  Power_plug1 = Power plug

nets:
  N1: C1.-, ESP8266.pin4, USBSerial.pin3, R1.Pin_1, Sensor.pin3, C2.-, J4.pin1, Power_plug1.GND
  N2: C1.+, U1.IN, Sensor.pin1, Power_plug1.VCC
  N3: ESP8266.pin1, USBSerial.pin5
  N4: ESP8266.pin2, J4.pin2
  N5: ESP8266.pin5, USBSerial.pin4
  N6: ESP8266.pin6, ESP8266.pin8, R2.Pin_1, U1.OUT, C2.+
  N7: R2.Pin_0, R1.Pin_0, U1.ADJ
  N8: Sensor.pin2, J4.pin3

custom parts:
  Electrolytic Capacitor: A small electrolytic capacitor
